// Logisim project cpu.circ as structural Verilog: 10 circuits, main circuit cpu
module cpu (
  input  clk,
  input  ram_end,
  input  clr,
  input  [31:0] ram_data,
  output [31:0] ram_read_addr,
  output cpu_end,
  output [31:0] ram_read_addr_2,
  output need_read,
  output halt,
  output tty_enable,
  output [6:0] tty_out
);

  wire and_1_out, beq, bgtz, blez, bltz, bneq, cpu_end_0, cpu_end_1, data_path_1_even,
       data_path_1_negative_flag, data_path_1_zero_flag, \end , eq, fin, greater, hypothesis, immediate,
       is_comparission, is_copy, is_hilo, is_jump, J, JR, less, LW, not_1_out, not_2_out, not_3_out,
       not_4_out, on_memory, or_1_out, or_2_out, or_3_out, or_4_out, or_5_out, POP, rw, SHi, SLo, SP_plus,
       zero;
  wire [1:0] data_selector;
  wire [2:0] hypothesis_jump_selector_1_s0;
  wire [3:0] alu_selector;
  wire [4:0] DA, multiplexer_2_out, multiplexer_10_out, register_d, register_s, register_t;
  wire [5:0] func_code, op_code;
  wire [15:0] multiplexer_1_out, offset;
  wire [25:0] jump;
  wire [31:0] adder_2_out, B, bit_extender_1_out, \const , const2, constant, constant_2, constt2, fromRam,
       Hi, hi_t, instruction, Lo, lo_t, multiplexer_3_out, multiplexer_4_out, multiplexer_6_out,
       multiplexer_11_out, pc_next, ram;
  wire [31:7] A;

  Multiplexer #(.width(16)) multiplexer_1 (
    .in0({16{1'b0}}), .in1(offset), .out(multiplexer_1_out), .sel(hypothesis));  // open: en
  and and_1 (and_1_out, fin, ~SP_plus);  // AND_Gate
  not not_1 (not_1_out, halt);
  Multiplexer #(.width(5)) multiplexer_2 (
    .in0(register_d), .in1(register_t), .out(multiplexer_2_out), .sel(or_1_out));  // open: en
  or or_1 (or_1_out, immediate, LW);
  Multiplexer #(.width(32), .enable("false")) multiplexer_3 (
    .in0({32{1'b0}}), .in1(32'h1), .out(multiplexer_3_out), .sel(greater));
  Multiplexer #(.width(32), .enable("false")) multiplexer_4 (
    .in0({32{1'b0}}), .in1(32'h1), .out(multiplexer_4_out), .sel(greater));
  Register #(.width(32)) PC (.D(pc_next), .en(and_1_out), .Q(ram_read_addr), .clk(clk), .clr(clr));
  and and_2 (\end , ram_end, not_1_out);
  Multiplexer #(.width(5)) multiplexer_5 (
    .in0(multiplexer_2_out), .in1({5{1'b1}}), .out(DA), .sel(SP_plus));  // open: en
  Multiplexer #(.width(32)) multiplexer_6 (
    .in0(multiplexer_3_out), .in1(multiplexer_4_out), .out(multiplexer_6_out), .sel(immediate));  // open: en
  branch_control branch_control_1 (
    .PC_in(ram_read_addr), .jump(is_jump), .flag(hypothesis), .offset(multiplexer_1_out), .PC_out(pc_next),
    .J(J), .JR(JR), .constant(jump), .R_s({A, tty_out}));
  D_Flip_Flop d_ff_1 (.clk(clk), .D(\end ), .Q(fin));  // open: Qn, preset, en, reset
  Demultiplexer demultiplexer_1 (.out0(cpu_end_0), .out1(SP_plus), .in(fin), .sel(POP));  // open: en
  Register #(.width(32)) register_1 (.D(ram_data), .en(not_2_out), .Q(instruction), .clk(clk), .clr(clr));
  not not_2 (not_2_out, need_read);
  Multiplexer #(.width(32)) multiplexer_7 (
    .in0(constant), .in1(multiplexer_6_out), .out(const2), .sel(is_comparission));  // open: en
  is_tty is_tty_1 (.opcode(op_code), .is_tty(tty_enable), .funcode(func_code), .CLK(clk), .END(fin));
  instruction_decoder instruction_decoder_1 (
    .instruction(instruction), .op_code(op_code), .Rs(register_s), .Rt(register_t), .Rd(register_d),
    .func_code(func_code), .constant(\const ), .jump(jump), .alu_selector(alu_selector),
    .immediate(immediate), .d_in_selector(data_selector), .data_path_rw(rw), .halt(halt),
    .comparisiion(is_comparission), .is_jump(is_jump), .is_copy(is_copy), .is_on_memory(on_memory), .LW(LW),
    .POP(POP), .offset(offset));
  D_Flip_Flop d_ff_2 (.clk(clk), .D(SP_plus), .Q(cpu_end_1));  // open: Qn, preset, en, reset
  Multiplexer #(.width(32)) multiplexer_8 (.in0(\const ), .in1({32{1'b0}}), .out(constant), .sel(zero));  // open: en
  is_hilo is_hilo_1 (
    .a6(func_code[0]), .a5(func_code[1]), .a4(func_code[2]), .a3(func_code[3]), .a2(func_code[4]),
    .a1(func_code[5]), .s1(is_hilo));
  and and_3 (need_read, or_2_out, not_3_out);
  or or_2 (or_2_out, LW, POP);
  Hi_Lo hi_lo_1 (
    .OP0(op_code[0]), .OP1(op_code[1]), .OP2(op_code[2]), .OP3(op_code[3]), .OP4(op_code[4]),
    .OP5(op_code[5]), .F0(func_code[0]), .F1(func_code[1]), .F2(func_code[2]), .F3(func_code[3]),
    .F4(func_code[4]), .F5(func_code[5]), .SHi(SHi), .SLo(SLo));
  Adder #(.width(32)) adder_1 (.a({A, tty_out}), .b(bit_extender_1_out), .out(fromRam));  // open: cin, cout
  assign bit_extender_1_out = {{16{offset[15]}}, offset};  // Bit_Extender bit_extender_1
  not not_3 (not_3_out, cpu_end);
  Multiplexer #(.select(2), .width(32)) multiplexer_9 (
    .in0(const2), .in1(Hi), .in2(Lo), .out(constt2), .sel({SLo, SHi}));  // open: in3, en
  Multiplexer #(.width(5)) multiplexer_10 (
    .in0(register_t), .in1({5{1'b1}}), .out(multiplexer_10_out), .sel(POP));  // open: en
  Register #(.width(32)) u_Hi (.D(hi_t), .en(is_hilo), .Q(Hi), .clk(clk));  // open: clr
  Register #(.width(32)) u_Lo (.D(lo_t), .en(is_hilo), .Q(Lo), .clk(clk));  // open: clr
  data_path data_path_1 (
    .s_a(register_s), .s_b(multiplexer_10_out), .dest_addr(DA), .constant(constant), .Ram(ram),
    .zero_flag(data_path_1_zero_flag), .negative_flag(data_path_1_negative_flag), .is_immediate(or_4_out),
    .d_in_selector(data_selector), .rst(clr), .greater(greater), .alu_selector(alu_selector), .equal(eq),
    .less(less), .even(data_path_1_even), .rw(rw), .enable(fin), .constant_2(constant_2), .A({A, tty_out}),
    .B(B), .lo(lo_t), .hi(hi_t));
  Multiplexer #(.width(32)) multiplexer_11 (
    .in0(constt2), .in1(ram_data), .out(multiplexer_11_out), .sel(or_3_out));  // open: en
  or or_3 (or_3_out, LW, POP);
  Adder #(.width(32)) adder_2 (.a(B), .b(32'h4), .out(adder_2_out));  // open: cin, cout
  or or_4 (or_4_out, immediate, zero);
  Multiplexer #(.width(32)) multiplexer_12 (
    .in0(multiplexer_11_out), .in1(adder_2_out), .out(constant_2), .sel(SP_plus));  // open: en
  Multiplexer multiplexer_13 (.in0(1'b0), .in1(1'b1), .out(beq), .sel(eq));  // open: en
  Multiplexer multiplexer_14 (.in0(1'b0), .in1(1'b1), .out(bneq), .sel(not_4_out));  // open: en
  not not_4 (not_4_out, eq);
  Multiplexer multiplexer_15 (.in0(1'b0), .in1(1'b1), .out(blez), .sel(or_5_out));  // open: en
  or or_5 (or_5_out, greater, eq);
  Multiplexer multiplexer_16 (.in0(1'b0), .in1(1'b1), .out(bgtz), .sel(less));  // open: en
  Multiplexer multiplexer_17 (.in0(1'b0), .in1(1'b1), .out(bltz), .sel(greater));  // open: en
  Multiplexer #(.width(32)) multiplexer_18 (.in0(fromRam), .in1(B), .out(ram_read_addr_2), .sel(POP));  // open: en
  hypothesis_jump_selector hypothesis_jump_selector_1 (
    .Op0(op_code[0]), .Op1(op_code[1]), .Op2(op_code[2]), .Op3(op_code[3]), .Op4(op_code[4]),
    .Op5(op_code[5]), .F0(func_code[0]), .F1(func_code[1]), .F2(func_code[2]), .F3(func_code[3]),
    .F4(func_code[4]), .F5(func_code[5]), .S0(hypothesis_jump_selector_1_s0[0]),
    .S1(hypothesis_jump_selector_1_s0[1]), .S2(hypothesis_jump_selector_1_s0[2]), .ZERO(zero), .J(J), .Jr(JR));
  or or_6 (cpu_end, cpu_end_0, cpu_end_1);
  Multiplexer #(.select(3), .enable("false")) multiplexer_19 (
    .in0(beq), .in1(bneq), .in2(blez), .in3(bgtz), .in4(bltz), .out(hypothesis),
    .sel(hypothesis_jump_selector_1_s0));  // open: in5, in6, in7
  // Probe on hypothesis_jump_selector_1_s0

  // Other names for the same wires on the sheet: A[6:0] = tty_out; pc_current[31:0] = ram_read_addr;
  //   RAMDATA[31:0] = ram_data; read_from_ram = need_read

  // Notes on the sheet:
  //   D.ADDRESS
  //   COMPARISSIONS
  //   COPY FROM Hi/Lo
  //   MEMORY_INST
  //   JUMPS
endmodule

module cpu_test (
);

  wire clock_1_out, \end , fake_ram_1_end;
  wire [31:0] addr, fake_ram_1_data;

  fake_ram fake_ram_1 (
    .cycles(4'b0011), .clk(clock_1_out), .db0(32'h1), .db1(32'h2), .db2(32'h3), .db3(32'h4), .ad(addr),
    .data(fake_ram_1_data), .\end (fake_ram_1_end), .cpu_end(\end ));  // open: real_addr, CLR
  // Probe on fake_ram_1_data
  Clock clock_1 (.out(clock_1_out));
  cpu cpu_1 (
    .ram_end(fake_ram_1_end), .ram_data(fake_ram_1_data), .ram_read_addr(addr), .clk(clock_1_out),
    .cpu_end(\end ));  // open: ram_read_addr_2, need_read, halt, clr, tty_enable, tty_out
  // Probe on addr
endmodule

module fake_ram (
  input  [3:0] cycles,
  input  clk,
  input  [31:0] db0,
  input  cpu_end,
  input  [31:0] db1,
  input  [31:0] db2,
  input  [31:0] db3,
  input  [31:0] ad,
  input  CLR,
  output [31:0] data,
  output \end ,
  output [15:0] real_addr
);

  wire or_1_out;
  wire [1:0] db_flag;
  wire [31:0] blocks;
  wire [31:2] divider_2_out;
  wire [31:16] arddr;

  Divider #(.width(32)) divider_1 (.a(ad), .b(32'h10), .out({arddr, real_addr}), .rem(blocks));  // open: upper
  Multiplexer #(.select(2), .width(32), .enable("false")) multiplexer_1 (
    .in0(db0), .in1(db1), .in2(db2), .in3(db3), .out(data), .sel(db_flag));
  Divider #(.width(32)) divider_2 (.a(blocks), .b(32'h4), .out({divider_2_out, db_flag}));  // open: upper, rem
  waita waita_1 (.cycles(cycles), .clk(clk), .cpu_end(or_1_out), .\end (\end ));
  or or_1 (or_1_out, cpu_end, CLR);

  // Other names for the same wires on the sheet: arddr[15:0] = real_addr; real_arddr[15:0] = real_addr
endmodule

module waita (
  input  clk,
  input  [3:0] cycles,
  input  cpu_end,
  output \end 
);

  wire not_1_out;
  wire [3:0] counter_1_q;

  Counter #(.width(4), .max('hf)) counter_1 (
    .count(not_1_out), .Q(counter_1_q), .clk(clk), .clr(cpu_end));  // open: load, D, carry
  not not_1 (not_1_out, \end );
  Comparator #(.width(4)) comparator_1 (.a(counter_1_q), .b(cycles), .eq(\end ));  // open: gt, lt
endmodule

module hypothesis_jump_selector (
  input  Op0,
  input  Op1,
  input  Op2,
  input  Op3,
  input  Op4,
  input  Op5,
  input  F0,
  input  F1,
  input  F2,
  input  F3,
  input  F4,
  input  F5,
  output S0,
  output S1,
  output S2,
  output ZERO,
  output J,
  output Jr
);

  wire and_4_out, and_5_out, not_1_out, not_2_out, not_3_out, not_4_out, not_5_out, not_6_out, not_7_out,
       not_8_out, not_9_out, not_10_out, not_11_out, not_12_out, not_13_out, not_14_out, not_15_out,
       not_16_out, not_17_out, not_18_out, not_19_out, not_20_out, not_21_out, not_22_out, not_23_out,
       not_24_out, not_25_out, not_26_out, not_27_out, not_28_out, not_29_out, not_30_out, not_31_out,
       not_32_out, not_33_out, not_34_out, not_35_out;

  not not_1 (not_1_out, Op1);
  not not_2 (not_2_out, Op2);
  not not_3 (not_3_out, Op3);
  not not_4 (not_4_out, Op4);
  not not_5 (not_5_out, Op5);
  not not_6 (not_6_out, Op3);
  not not_7 (not_7_out, Op4);
  not not_8 (not_8_out, Op5);
  not not_9 (not_9_out, Op3);
  not not_10 (not_10_out, Op4);
  not not_11 (not_11_out, Op5);
  not not_12 (not_12_out, Op3);
  not not_13 (not_13_out, Op4);
  not not_14 (not_14_out, Op5);
  not not_15 (not_15_out, Op1);
  not not_16 (not_16_out, Op2);
  not not_17 (not_17_out, Op3);
  not not_18 (not_18_out, Op4);
  not not_19 (not_19_out, Op5);
  not not_20 (not_20_out, Op0);
  not not_21 (not_21_out, Op2);
  not not_22 (not_22_out, Op3);
  not not_23 (not_23_out, Op4);
  not not_24 (not_24_out, Op5);
  not not_25 (not_25_out, Op0);
  not not_26 (not_26_out, Op1);
  not not_27 (not_27_out, Op2);
  not not_28 (not_28_out, Op3);
  not not_29 (not_29_out, Op4);
  not not_30 (not_30_out, Op5);
  not not_31 (not_31_out, F0);
  not not_32 (not_32_out, F1);
  not not_33 (not_33_out, F2);
  not not_34 (not_34_out, F4);
  not not_35 (not_35_out, F5);
  and and_1 (S0, Op0, not_1_out, not_2_out, not_3_out, not_4_out, not_5_out);
  and and_2 (S1, Op1, Op2, not_6_out, not_7_out, not_8_out);
  and and_3 (S2, Op0, Op2, not_9_out, not_10_out, not_11_out);
  and and_4 (and_4_out, Op1, Op2, not_12_out, not_13_out, not_14_out);
  and and_5 (and_5_out, Op0, not_15_out, not_16_out, not_17_out, not_18_out, not_19_out);
  and and_6 (J, not_20_out, Op1, not_21_out, not_22_out, not_23_out, not_24_out);
  and and_7 (Jr, not_25_out, not_26_out, not_27_out, not_28_out, not_29_out, not_30_out, not_31_out, not_32_out, not_33_out, F3, not_34_out, not_35_out);
  or or_1 (ZERO, and_4_out, and_5_out);
endmodule

module Hi_Lo (
  input  OP0,
  input  OP1,
  input  OP2,
  input  OP3,
  input  OP4,
  input  OP5,
  input  F0,
  input  F1,
  input  F2,
  input  F3,
  input  F4,
  input  F5,
  output SHi,
  output SLo
);

  wire not_1_out, not_2_out, not_3_out, not_4_out, not_5_out, not_6_out, not_7_out, not_8_out, not_9_out,
       not_10_out, not_11_out, not_12_out, not_13_out, not_14_out, not_15_out, not_16_out, not_17_out,
       not_18_out, not_19_out, not_20_out, not_21_out;

  not not_1 (not_1_out, OP0);
  not not_2 (not_2_out, OP1);
  not not_3 (not_3_out, OP2);
  not not_4 (not_4_out, OP3);
  not not_5 (not_5_out, OP4);
  not not_6 (not_6_out, OP5);
  not not_7 (not_7_out, F0);
  not not_8 (not_8_out, F1);
  not not_9 (not_9_out, F2);
  not not_10 (not_10_out, F3);
  not not_11 (not_11_out, F5);
  not not_12 (not_12_out, OP0);
  not not_13 (not_13_out, OP1);
  not not_14 (not_14_out, OP2);
  not not_15 (not_15_out, OP3);
  not not_16 (not_16_out, OP4);
  not not_17 (not_17_out, OP5);
  not not_18 (not_18_out, F0);
  not not_19 (not_19_out, F2);
  not not_20 (not_20_out, F3);
  not not_21 (not_21_out, F5);
  and and_1 (SHi, not_1_out, not_2_out, not_3_out, not_4_out, not_5_out, not_6_out, not_7_out, not_8_out, not_9_out, not_10_out, F4, not_11_out);
  and and_2 (SLo, not_12_out, not_13_out, not_14_out, not_15_out, not_16_out, not_17_out, not_18_out, F1, not_19_out, not_20_out, F4, not_21_out);
endmodule

module is_tty (
  input  [5:0] opcode,
  input  [5:0] funcode,
  input  CLK,
  input  END,
  output is_tty
);

  wire all_true_1_s1, and_1_out, and_2_out, and_3_out, MAX, one_1_s1;

  all_true all_true_1 (
    .i1(opcode[0]), .i2(opcode[1]), .i3(opcode[2]), .i4(opcode[3]), .i5(opcode[4]), .i6(opcode[5]),
    .s1(all_true_1_s1));
  one one_1 (
    .i1(funcode[0]), .i2(funcode[1]), .i3(funcode[2]), .i4(funcode[3]), .i5(funcode[4]), .i6(funcode[5]),
    .s1(one_1_s1));
  and and_1 (and_1_out, all_true_1_s1, one_1_s1);
  and and_2 (and_2_out, and_1_out, ~MAX);  // AND_Gate
  Counter #(.width(1), .max('h1)) counter_1 (.count(and_2_out), .carry(MAX), .clk(CLK), .clr(END));  // open: load, D, Q
  and and_3 (and_3_out, and_1_out, ~MAX);  // AND_Gate
  and and_4 (is_tty, END, and_3_out);
endmodule

module all_true (
  input  i1,
  input  i2,
  input  i3,
  input  i4,
  input  i5,
  input  i6,
  output s1
);

  and and_1 (s1, i1, i2, i3, i4, i5, i6);
endmodule

module one (
  input  i1,
  input  i2,
  input  i3,
  input  i4,
  input  i5,
  input  i6,
  output s1
);

  wire not_1_out, not_2_out, not_3_out, not_4_out, not_5_out;

  not not_1 (not_1_out, i2);
  not not_2 (not_2_out, i3);
  not not_3 (not_3_out, i4);
  not not_4 (not_4_out, i5);
  not not_5 (not_5_out, i6);
  and and_1 (s1, i1, not_1_out, not_2_out, not_3_out, not_4_out, not_5_out);
endmodule

module is_hilo (
  input  a6,
  input  a5,
  input  a4,
  input  a3,
  input  a2,
  input  a1,
  output s1
);

  wire not_1_out, not_2_out;

  not not_1 (not_1_out, a1);
  not not_2 (not_2_out, a4);
  and and_1 (s1, not_1_out, a2, a3, not_2_out);
endmodule
