// Logisim project data_path.circ as structural Verilog
module ALU (
  input  [31:0] A,
  input  [31:0] B,
  input  [3:0] S,
  output [31:0] R,
  output Zero,
  output Neg
);

  wire [31:0] adder_1_out, and_1_out, divider_1_out, multiplier_1_out, or_1_out, shifter_1_out,
       shifter_2_out, subtractor_1_out;

  Comparator #(.width(32)) comparator_1 (.a({Neg, R[30:0]}), .b({32{1'b0}}), .eq(Zero));  // open: gt, lt
  Adder #(.width(32)) adder_1 (.a(A), .b(B), .out(adder_1_out));  // open: cin, cout
  Subtractor #(.width(32)) subtractor_1 (.a(A), .b(B), .out(subtractor_1_out));  // open: bin, bout
  Multiplier #(.width(32)) multiplier_1 (.a(A), .b(B), .out(multiplier_1_out));  // open: cin, cout
  Divider #(.width(32)) divider_1 (.a(A), .b(B), .out(divider_1_out));  // open: upper, rem
  assign and_1_out = A & B;  // AND_Gate and_1, 32 bits wide
  assign or_1_out = A | B;  // OR_Gate or_1, 32 bits wide
  Shifter #(.width(32)) shifter_1 (.in(A), .\dist ({5{1'b1}}), .out(shifter_1_out));
  Shifter #(.width(32), .shift("lr")) shifter_2 (.in(A), .\dist ({5{1'b1}}), .out(shifter_2_out));
  Multiplexer #(.select(4), .width(32), .enable("false")) multiplexer_1 (
    .in0(adder_1_out), .in1(subtractor_1_out), .in2(multiplier_1_out), .in3(divider_1_out), .in4(and_1_out),
    .in5(or_1_out), .in6(shifter_1_out), .in7(shifter_2_out), .in13({32{1'b1}}), .in15({32{1'b0}}),
    .out({Neg, R[30:0]}), .sel(S));  // open: in8, in9, in10, in11, in12, in14

  assign R[31] = Neg;

  // Other names for the same wires on the sheet: res[31:0] = {Neg, R[30:0]}
endmodule

module register_file (
  input  [4:0] DA,
  input  [31:0] DI,
  input  R_W,
  input  [4:0] SA,
  input  [4:0] SB,
  input  Clk,
  input  Reset,
  output [31:0] A,
  output [31:0] B
);

  wire w1, w2;
  wire [31:0] r1, r2;

  Multiplexer #(.select(5), .width(32), .enable("false")) multiplexer_1 (
    .in0(r1), .in1(r2), .out(A), .sel(SA));  // open: in2, in3, in4, in5, in6, in7, in8, in9, in10, in11, in12, in13, in14, in15, in16, in17, in18, in19, in20, in21, in22, in23, in24, in25, in26, in27, in28, in29, in30, in31
  Register #(.width(32)) register_1 (.D(DI), .en(w1), .Q(r1), .clk(Clk), .clr(Reset));
  Register #(.width(32)) register_2 (.D(DI), .en(w2), .Q(r2), .clk(Clk), .clr(Reset));
  // Probe on A
  Multiplexer #(.select(5), .width(32), .enable("false")) multiplexer_2 (
    .in0(r1), .in1(r2), .out(B), .sel(SB));  // open: in2, in3, in4, in5, in6, in7, in8, in9, in10, in11, in12, in13, in14, in15, in16, in17, in18, in19, in20, in21, in22, in23, in24, in25, in26, in27, in28, in29, in30, in31
  // Probe on B
  Demultiplexer #(.select(5), .disabled(0)) demultiplexer_1 (
    .out0(w1), .out1(w2), .in(1'b1), .sel(DA), .en(R_W));  // open: out2, out3, out4, out5, out6, out7, out8, out9, out10, out11, out12, out13, out14, out15, out16, out17, out18, out19, out20, out21, out22, out23, out24, out25, out26, out27, out28, out29, out30, out31

  // Other names for the same wires on the sheet: rst = Reset; w = R_W

  // Notes on the sheet:
  //   Inputs
  //   Data Address
  //   Data In
  //   Read/Write
  //   Selector A
  //   Selector B
  //   pincha con el 1 porque r/w es el enable
  //   Outputs
  //   Data A
  //   Data B
endmodule

module data_path (
  input  [4:0] in_1,
  input  [31:0] in_2,
  input  [4:0] in_3,
  input  [4:0] in_4,
  input  in_5,
  input  in_6,
  input  [31:0] in_7,
  input  [3:0] in_8
);

  wire clock_1_out;
  wire [31:0] alu_1_r, register_file_1_a, register_file_1_b;

  // Probe on alu_1_r
  register_file register_file_1 (
    .DA(in_4), .DI(alu_1_r), .R_W(in_5), .SA(in_1), .SB(in_3), .Clk(clock_1_out), .Reset(in_6),
    .A(register_file_1_a), .B(register_file_1_b));
  Clock clock_1 (.out(clock_1_out));
  // Probe on register_file_1_a
  // Probe on register_file_1_b
  ALU alu_1 (.A(register_file_1_a), .B(register_file_1_b), .S(in_8), .R(alu_1_r));  // open: Zero, Neg
endmodule
